// Logisim project control_logic.circ as structural Verilog: 1 circuit, main circuit control_logic
module control_logic (
  input  [31:0] inst,
  input  BrEq,
  input  BrLt,
  output PCSel,
  output RegWEn,
  output [2:0] ImmSel,
  output BrUn,
  output ASel,
  output BSel,
  output [3:0] ALUSel,
  output MemRW,
  output [1:0] WBSel,
  output CSRSel,
  output CSRWen
);

  wire and_5_out, and_6_out, and_7_out, and_8_out, and_9_out, and_10_out, and_11_out, and_12_out, and_13_out,
       and_14_out, blt, bltu, decoder_1_out0, decoder_1_out1, decoder_1_out2, decoder_1_out3, decoder_1_out4,
       decoder_1_out5, decoder_1_out6, decoder_1_out7, HEX00, HEX01, HEX20, multiplexer_1_out, not_1_out,
       not_2_out, not_3_out, not_4_out, not_5_out, not_6_out, not_7_out, not_8_out, not_9_out, not_10_out,
       not_11_out, not_12_out, not_13_out, not_14_out, not_15_out, not_16_out, not_17_out, not_18_out,
       not_19_out, not_20_out;

  not not_1 (not_1_out, inst[12]);
  and and_1 (BrUn, not_1_out, inst[13], inst[14]);
  not not_2 (not_2_out, inst[2]);
  not not_3 (not_3_out, inst[3]);
  not not_4 (not_4_out, inst[6]);
  not not_5 (not_5_out, inst[2]);
  not not_6 (not_6_out, inst[3]);
  not not_7 (not_7_out, inst[4]);
  not not_8 (not_8_out, inst[6]);
  nand nand_1 (BSel, inst[0], inst[1], not_2_out, not_3_out, inst[4], inst[5], not_4_out);
  and and_2 (MemRW, inst[0], inst[1], not_5_out, not_6_out, not_7_out, inst[5], not_8_out);
  not not_9 (not_9_out, inst[2]);
  not not_10 (not_10_out, inst[3]);
  not not_11 (not_11_out, inst[4]);
  not not_12 (not_12_out, BrUn);
  and and_3 (bltu, BrLt, BrUn);
  and and_4 (blt, BrLt, not_12_out);
  not not_13 (not_13_out, inst[4]);
  not not_14 (not_14_out, inst[3]);
  not not_15 (not_15_out, inst[4]);
  and and_5 (and_5_out, inst[0], inst[1], not_9_out, not_10_out, not_11_out, inst[5], inst[6]);
  and and_6 (and_6_out, inst[0], inst[1], inst[2], inst[3], not_13_out, inst[5], inst[6]);
  and and_7 (and_7_out, inst[0], inst[1], inst[2], not_14_out, not_15_out, inst[5], inst[6]);
  not not_16 (not_16_out, BrEq);
  not not_17 (not_17_out, blt);
  not not_18 (not_18_out, bltu);
  Multiplexer #(.select(3)) multiplexer_1 (
    .in0(BrEq), .in1(not_16_out), .in4(blt), .in5(not_17_out), .in6(bltu), .in7(not_18_out),
    .out(multiplexer_1_out), .sel(inst[14:12]), .en(and_5_out));  // open: in2, in3
  or or_1 (PCSel, multiplexer_1_out, and_6_out, and_7_out);
  not not_19 (not_19_out, inst[25]);
  not not_20 (not_20_out, inst[30]);
  nor nor_1 (HEX00, inst[25], inst[26], inst[27], inst[28], inst[29], inst[30], inst[31]);
  nor nor_2 (HEX01, not_19_out, inst[26], inst[27], inst[28], inst[29], inst[30], inst[31]);
  nor nor_3 (HEX20, inst[25], inst[26], inst[27], inst[28], inst[29], not_20_out, inst[31]);
  Decoder #(.select(3)) decoder_1 (
    .out0(decoder_1_out0), .out1(decoder_1_out1), .out2(decoder_1_out2), .out3(decoder_1_out3),
    .out4(decoder_1_out4), .out5(decoder_1_out5), .out6(decoder_1_out6), .out7(decoder_1_out7),
    .sel(inst[14:12]), .en(1'b1));
  and and_8 (and_8_out, decoder_1_out0, HEX00);
  and and_9 (and_9_out, decoder_1_out0, HEX01);
  and and_10 (and_10_out, decoder_1_out5, HEX00);
  and and_11 (and_11_out, decoder_1_out5, HEX20);
  and and_12 (and_12_out, decoder_1_out0, HEX20);
  Priority_Encoder #(.select(4)) priority_encoder_1 (
    .in0(and_8_out), .in1(decoder_1_out7), .in2(decoder_1_out6), .in3(decoder_1_out4), .in4(and_10_out),
    .in5(and_11_out), .in6(and_13_out), .in7(decoder_1_out2), .in10(and_9_out), .in11(decoder_1_out3),
    .in12(and_12_out), .in13(BSel), .in14(and_14_out), .out(ALUSel));  // open: in8, in9, in15
  and and_13 (and_13_out, decoder_1_out1, HEX00);
  and and_14 (and_14_out, decoder_1_out1, HEX01);

  // Other names for the same wires on the sheet: opcode[6:0] = inst[6:0]; rd[4:0] = inst[11:7];
  //   funct3[2:0] = inst[14:12]; rs1[4:0] = inst[19:15]; rs2[4:0] = inst[24:20]; funct7[6:0] = inst[31:25]

  // Notes on the sheet:
  //   INPUTS to your circuit
  //   DON'T CHANGE THE LOCATIONS OF THE INPUTS AND OUTPUTS!
  //   OUTPUT from your circuit
  //   R-Type opcode=0x33->BSel=0
  //   B-Type opcode=0x63
  //   UJ-Type opcode=0x6f
  //   I-Type opcode=0x67
  //   The logic of PCSel
  //   The logic of ALUSel
endmodule
