// Logisim project imm_gen.circ as structural Verilog: 1 circuit, main circuit imm_gen
module imm_gen (
  input  [31:0] inst,
  input  [2:0] ImmSel,
  output [31:0] imm
);

  wire [31:11] immi, imms;
  wire [31:12] immsb;
  wire [31:20] immuj;

  assign immi = {{20{inst[31]}}, inst[31]};  // Bit_Extender bit_extender_1
  assign imms = {{20{inst[31]}}, inst[31]};  // Bit_Extender bit_extender_2
  assign immsb = {{19{inst[31]}}, inst[31]};  // Bit_Extender bit_extender_3
  assign immuj = {{11{inst[31]}}, inst[31]};  // Bit_Extender bit_extender_4

  // Other names for the same wires on the sheet: imms[10:0] = {inst[30:25], inst[11:7]};
  //   immsb[11:1] = {inst[7], inst[30:25], inst[11:8]}; immu[31:12] = inst[31:12]; immi[10:0] = inst[30:20];
  //   immuj[19:1] = {inst[19:12], inst[20], inst[30:21]}

  // Notes on the sheet:
  //   INPUTS to your circuit
  //   DON'T CHANGE THE LOCATIONS OF THE INPUTS AND OUTPUTS!
  //   OUTPUT from your circuit
endmodule
